# Fritzing sketch IMU-Joystick_with_HC-SR04 (saved by Fritzing 0.9.3b)
breadboards: 1

parts:
  GY2 = GY-521 (MPU-6050) [form="♀ (female)" package=THT]
  S1 = Momentary Switch [package=ksa_sealed_tac_switch]
  Pro_Micro1 = SparkFun Pro Micro
  hc-sr1 = hc-sr04  # not connected

nets:
  N1: GY2.pin1, Pro_Micro1.VCC
  N2: GY2.pin2, S1.3, S1.4, Pro_Micro1.GND
  N3: GY2.pin3, Pro_Micro1.3
  N4: GY2.pin4, Pro_Micro1.2
  N5: GY2.pin6, Pro_Micro1.9
  N6: GY2.pin7, Pro_Micro1.8
  N7: GY2.pin8, Pro_Micro1.7
  N8: S1.1, S1.2, Pro_Micro1.10

custom parts:
  GY-521 (MPU-6050): Placa GY-521 basada en conjunto de acelerómetro+giroscopios MPU-6050
  SparkFun Pro Micro: The Pro Micro is similar to the Pro Mini except with an ATmega32U4 on board. The USB transceiver inside the 32U4 allows us to add USB connectivity on-board and do away with bulky external USB interface. Based on: https://github.com/unorthodox-engineers/unorthodox-arduino/blob/master/Unorthodox/fritzing/parts/Pro%20Micro.fzpz
